// Logisim project tictactoe_with_extensions.circ as structural Verilog: 6 circuits, main circuit main
module main (
);

  wire and_2_out, and_3_out, and_4_out, buffer_1_out, buffer_2_out, buffer_3_out, buffer_4_out, buffer_5_out,
       button_1_out, button_2_out, button_3_out, button_4_out, button_5_out, button_6_out, button_7_out,
       button_8_out, button_9_out, cdm_8_mark5_1_p1, cdm_8_mark5_1_p2, cdm_8_mark5_1_p4, cdm_8_mark5_1_p5,
       cdm_8_mark5_1_p6, cdm_8_mark5_1_p7, cdm_8_mark5_1_p8, cdm_8_mark5_1_p9, cdm_8_mark5_1_p10, clk,
       correctness_turn_driver_1_bad, correctness_turn_driver_1_good, decoder_1_out0, decoder_1_out1,
       decoder_2_out0, decoder_2_out1, game_state_display_driver_1_draw,
       game_state_display_driver_1_end_of_game, game_state_display_driver_1_loss,
       game_state_display_driver_1_win, In_out, IOsel, not_1_out, not_2_out, reset;
  wire [1:0] symbol_display_router_1_hor_bus0, symbol_display_router_1_hor_bus1,
       symbol_display_router_1_hor_bus2, symbol_display_router_1_ver_bus0, symbol_display_router_1_ver_bus1,
       symbol_display_router_1_ver_bus2;
  wire [2:2] ttt_cell_1_hor_out, ttt_cell_1_ver_out, ttt_cell_2_hor_out, ttt_cell_3_hor_out,
       ttt_cell_4_ver_out, ttt_cell_7_ver_out;
  wire [3:0] IOadr, ttt_cell_1_row0, ttt_cell_1_row1, ttt_cell_1_row2, ttt_cell_1_row3, ttt_cell_2_row0,
       ttt_cell_2_row1, ttt_cell_2_row2, ttt_cell_2_row3, ttt_cell_3_row0, ttt_cell_3_row1, ttt_cell_3_row2,
       ttt_cell_3_row3, ttt_cell_4_row0, ttt_cell_4_row1, ttt_cell_4_row2, ttt_cell_4_row3, ttt_cell_5_row0,
       ttt_cell_5_row1, ttt_cell_5_row2, ttt_cell_5_row3, ttt_cell_6_row0, ttt_cell_6_row1, ttt_cell_6_row2,
       ttt_cell_6_row3, ttt_cell_7_row0, ttt_cell_7_row1, ttt_cell_7_row2, ttt_cell_7_row3, ttt_cell_8_row0,
       ttt_cell_8_row1, ttt_cell_8_row2, ttt_cell_8_row3, ttt_cell_9_row0, ttt_cell_9_row1, ttt_cell_9_row2,
       ttt_cell_9_row3;
  wire [7:0] button_press_capture_1_clean, cdm_8_mark5_1_p13, cdm_8_mark5_1_p14, IOdata;
  wire [7:4] cdm_8_mark5_1_p12;

  LED led_1 (.in(correctness_turn_driver_1_good));
  Clock clock_1 (.out(clk));
  // Probe on cdm_8_mark5_1_p2
  // Probe on cdm_8_mark5_1_p1
  LED led_2 (.in(game_state_display_driver_1_win));
  LED led_3 (.in(game_state_display_driver_1_draw));
  LED led_4 (.in(game_state_display_driver_1_loss));
  Game_State_Display_Driver game_state_display_driver_1 (
    .result(IOdata[7:6]), .sel(and_4_out), .win(game_state_display_driver_1_win),
    .loss(game_state_display_driver_1_loss), .draw(game_state_display_driver_1_draw), .reset(reset),
    .end_of_game(game_state_display_driver_1_end_of_game));
  Button u_reset (.out(reset));
  LED led_5 (.in(correctness_turn_driver_1_bad));
  Correctness_Turn_Driver correctness_turn_driver_1 (
    .IOdata(IOdata), .IOsel(IOsel), .IOadr(IOadr), .reset(reset), .good(correctness_turn_driver_1_good),
    .bad(correctness_turn_driver_1_bad));
  // Probe on cdm_8_mark5_1_p5
  // Probe on cdm_8_mark5_1_p4
  // Probe on cdm_8_mark5_1_p7
  // Probe on cdm_8_mark5_1_p6
  Symbol_Display_Router symbol_display_router_1 (
    .sel(and_4_out), .xy_crd(IOdata[5:2]), .Symbol_ID(IOdata[1:0]),
    .Hor_bus0(symbol_display_router_1_hor_bus0), .Hor_bus1(symbol_display_router_1_hor_bus1),
    .Hor_bus2(symbol_display_router_1_hor_bus2), .Ver_bus0(symbol_display_router_1_ver_bus0),
    .Ver_bus1(symbol_display_router_1_ver_bus1), .Ver_bus2(symbol_display_router_1_ver_bus2));
  and and_1 (IOsel, 1'b1, IOadr[1], ~IOadr[2], ~IOadr[3], cdm_8_mark5_1_p12[4], cdm_8_mark5_1_p12[5], cdm_8_mark5_1_p12[6], cdm_8_mark5_1_p12[7], decoder_1_out1);  // AND_Gate
  // Probe on cdm_8_mark5_1_p8
  Decoder #(.disabled(0)) decoder_1 (
    .out0(decoder_1_out0), .out1(decoder_1_out1), .sel(cdm_8_mark5_1_p9), .en(cdm_8_mark5_1_p10));
  // CdM_8_mark5 cdm_8_mark5_1: pin names not known; wires that end beside it: cdm_8_mark5_1_p1, cdm_8_mark5_1_p2, clk, cdm_8_mark5_1_p4, cdm_8_mark5_1_p5, cdm_8_mark5_1_p6, cdm_8_mark5_1_p7, cdm_8_mark5_1_p8, cdm_8_mark5_1_p9, cdm_8_mark5_1_p10, In_out, {cdm_8_mark5_1_p12, IOadr}, cdm_8_mark5_1_p13, cdm_8_mark5_1_p14
  not not_1 (not_1_out, In_out);
  assign IOdata = not_1_out ? cdm_8_mark5_1_p13 : 8'bz;  // Controlled_Buffer controlled_buffer_1
  assign cdm_8_mark5_1_p14 = In_out ? IOdata : 8'bz;  // Controlled_Buffer controlled_buffer_2
  buf buffer_1 (buffer_1_out, In_out);
  DotMatrix #(.inputtype("row"), .matrixcols(4), .matrixrows(4)) dotmatrix_1 (
    .row0(ttt_cell_1_row0), .row1(ttt_cell_1_row1), .row2(ttt_cell_1_row2), .row3(ttt_cell_1_row3));
  TTT_Cell ttt_cell_1 (
    .Hor_in(symbol_display_router_1_hor_bus0), .Ver_in(symbol_display_router_1_ver_bus0),
    .button(button_1_out), .Hor_out(ttt_cell_1_hor_out[2]), .row0(ttt_cell_1_row0), .row1(ttt_cell_1_row1),
    .row2(ttt_cell_1_row2), .row3(ttt_cell_1_row3), .Ver_out(ttt_cell_1_ver_out[2]), .reset(reset));
  TTT_Cell ttt_cell_2 (
    .Hor_in(symbol_display_router_1_hor_bus1), .Ver_in(symbol_display_router_1_ver_bus0),
    .button(button_2_out), .Hor_out(ttt_cell_2_hor_out[2]), .row0(ttt_cell_2_row0), .row1(ttt_cell_2_row1),
    .row2(ttt_cell_2_row2), .row3(ttt_cell_2_row3), .Ver_out(ttt_cell_1_ver_out[2]), .reset(reset));
  DotMatrix #(.inputtype("row"), .matrixcols(4), .matrixrows(4)) dotmatrix_2 (
    .row0(ttt_cell_2_row0), .row1(ttt_cell_2_row1), .row2(ttt_cell_2_row2), .row3(ttt_cell_2_row3));
  TTT_Cell ttt_cell_3 (
    .Hor_in(symbol_display_router_1_hor_bus2), .Ver_in(symbol_display_router_1_ver_bus0),
    .button(button_3_out), .Hor_out(ttt_cell_3_hor_out[2]), .row0(ttt_cell_3_row0), .row1(ttt_cell_3_row1),
    .row2(ttt_cell_3_row2), .row3(ttt_cell_3_row3), .Ver_out(ttt_cell_1_ver_out[2]), .reset(reset));
  DotMatrix #(.inputtype("row"), .matrixcols(4), .matrixrows(4)) dotmatrix_3 (
    .row0(ttt_cell_3_row0), .row1(ttt_cell_3_row1), .row2(ttt_cell_3_row2), .row3(ttt_cell_3_row3));
  and and_2 (and_2_out, decoder_1_out1, ~IOsel);  // AND_Gate
  buf buffer_2 (buffer_2_out, buffer_5_out);
  buf buffer_3 (buffer_3_out, buffer_4_out);
  buf buffer_4 (buffer_4_out, buffer_2_out);
  buf buffer_5 (buffer_5_out, buffer_1_out);
  Decoder #(.disabled(0)) decoder_2 (.out0(decoder_2_out0), .out1(decoder_2_out1), .sel(buffer_3_out), .en(and_3_out));
  and and_3 (and_3_out, IOsel, IOadr[0], IOadr[1], ~IOadr[2], ~IOadr[3]);  // AND_Gate
  and and_4 (and_4_out, decoder_2_out0, ~button_press_capture_1_clean[6]);  // AND_Gate
  Button button_1 (.out(button_1_out));
  Button button_2 (.out(button_2_out));
  Button button_3 (.out(button_3_out));
  // Probe on {cdm_8_mark5_1_p12, IOadr}
  DotMatrix #(.inputtype("row"), .matrixcols(4), .matrixrows(4)) dotmatrix_4 (
    .row0(ttt_cell_4_row0), .row1(ttt_cell_4_row1), .row2(ttt_cell_4_row2), .row3(ttt_cell_4_row3));
  TTT_Cell ttt_cell_4 (
    .Hor_in(symbol_display_router_1_hor_bus0), .Ver_in(symbol_display_router_1_ver_bus1),
    .button(button_4_out), .Hor_out(ttt_cell_1_hor_out[2]), .row0(ttt_cell_4_row0), .row1(ttt_cell_4_row1),
    .row2(ttt_cell_4_row2), .row3(ttt_cell_4_row3), .Ver_out(ttt_cell_4_ver_out[2]), .reset(reset));
  Button button_4 (.out(button_4_out));
  TTT_Cell ttt_cell_5 (
    .Hor_in(symbol_display_router_1_hor_bus1), .Ver_in(symbol_display_router_1_ver_bus1),
    .button(button_5_out), .Hor_out(ttt_cell_2_hor_out[2]), .row0(ttt_cell_5_row0), .row1(ttt_cell_5_row1),
    .row2(ttt_cell_5_row2), .row3(ttt_cell_5_row3), .Ver_out(ttt_cell_4_ver_out[2]), .reset(reset));
  DotMatrix #(.inputtype("row"), .matrixcols(4), .matrixrows(4)) dotmatrix_5 (
    .row0(ttt_cell_5_row0), .row1(ttt_cell_5_row1), .row2(ttt_cell_5_row2), .row3(ttt_cell_5_row3));
  Button button_5 (.out(button_5_out));
  TTT_Cell ttt_cell_6 (
    .Hor_in(symbol_display_router_1_hor_bus2), .Ver_in(symbol_display_router_1_ver_bus1),
    .button(button_6_out), .Hor_out(ttt_cell_3_hor_out[2]), .row0(ttt_cell_6_row0), .row1(ttt_cell_6_row1),
    .row2(ttt_cell_6_row2), .row3(ttt_cell_6_row3), .Ver_out(ttt_cell_4_ver_out[2]), .reset(reset));
  DotMatrix #(.inputtype("row"), .matrixcols(4), .matrixrows(4)) dotmatrix_6 (
    .row0(ttt_cell_6_row0), .row1(ttt_cell_6_row1), .row2(ttt_cell_6_row2), .row3(ttt_cell_6_row3));
  Button button_6 (.out(button_6_out));
  not not_2 (not_2_out, clk);
  TTT_Cell ttt_cell_7 (
    .Hor_in(symbol_display_router_1_hor_bus0), .Ver_in(symbol_display_router_1_ver_bus2),
    .button(button_7_out), .Hor_out(ttt_cell_1_hor_out[2]), .row0(ttt_cell_7_row0), .row1(ttt_cell_7_row1),
    .row2(ttt_cell_7_row2), .row3(ttt_cell_7_row3), .Ver_out(ttt_cell_7_ver_out[2]), .reset(reset));
  DotMatrix #(.inputtype("row"), .matrixcols(4), .matrixrows(4)) dotmatrix_7 (
    .row0(ttt_cell_7_row0), .row1(ttt_cell_7_row1), .row2(ttt_cell_7_row2), .row3(ttt_cell_7_row3));
  Button button_7 (.out(button_7_out));
  DotMatrix #(.inputtype("row"), .matrixcols(4), .matrixrows(4)) dotmatrix_8 (
    .row0(ttt_cell_8_row0), .row1(ttt_cell_8_row1), .row2(ttt_cell_8_row2), .row3(ttt_cell_8_row3));
  TTT_Cell ttt_cell_8 (
    .Hor_in(symbol_display_router_1_hor_bus1), .Ver_in(symbol_display_router_1_ver_bus2),
    .button(button_8_out), .Hor_out(ttt_cell_2_hor_out[2]), .row0(ttt_cell_8_row0), .row1(ttt_cell_8_row1),
    .row2(ttt_cell_8_row2), .row3(ttt_cell_8_row3), .Ver_out(ttt_cell_7_ver_out[2]), .reset(reset));
  Button button_8 (.out(button_8_out));
  TTT_Cell ttt_cell_9 (
    .Hor_in(symbol_display_router_1_hor_bus2), .Ver_in(symbol_display_router_1_ver_bus2),
    .button(button_9_out), .Hor_out(ttt_cell_3_hor_out[2]), .row0(ttt_cell_9_row0), .row1(ttt_cell_9_row1),
    .row2(ttt_cell_9_row2), .row3(ttt_cell_9_row3), .Ver_out(ttt_cell_7_ver_out[2]), .reset(reset));
  DotMatrix #(.inputtype("row"), .matrixcols(4), .matrixrows(4)) dotmatrix_9 (
    .row0(ttt_cell_9_row0), .row1(ttt_cell_9_row1), .row2(ttt_cell_9_row2), .row3(ttt_cell_9_row3));
  Button button_9 (.out(button_9_out));
  // Probe on IOdata
  RAM ram_1 (
    .addr({cdm_8_mark5_1_p12, IOadr}), .data(IOdata), .sel(and_2_out), .clk(not_2_out), .ld(In_out));  // open: clr
  ROM rom_1 (.addr({cdm_8_mark5_1_p12, IOadr}), .data(IOdata), .sel(decoder_1_out0));
  assign IOdata = decoder_2_out1 ? {button_press_capture_1_clean[7:6], 2'b00, button_press_capture_1_clean[3:0]} : 8'bz;  // Controlled_Buffer controlled_buffer_3
  Button_Press_Capture button_press_capture_1 (
    .Hor_bus2(ttt_cell_3_hor_out[2]), .XY(button_press_capture_1_clean[3:0]),
    .Hor_bus1(ttt_cell_2_hor_out[2]), .Hor_bus0(ttt_cell_1_hor_out[2]), .Ver_bus2(ttt_cell_7_ver_out[2]),
    .Ver_bus1(ttt_cell_4_ver_out[2]), .Ver_bus0(ttt_cell_1_ver_out[2]), .reset(decoder_2_out1),
    .ready(button_press_capture_1_clean[7]), .clean(button_press_capture_1_clean[6]), .button_reset(reset),
    .end_of_game(game_state_display_driver_1_end_of_game));

  // Notes on the sheet:
  //   loss | draw | win
  //   contents of rom_1 (hex, n*v repeats v):
  //   0 1 2 4 5 6 8 9 a 0 4 8 1 5 9 2 6 a 0 5 a 8 5 2 5 0 2 8 a 1 4 6 9 0 40 80 c0 0 1 2 0 1 2 d0 f0 c1 d1
  //   33 a4 c5 cd 0 d6 78 bd 5 e0 42 d1 2a d6 73 ee 34 ee 46 d1 29 d6 73 d6 d0 a e1 4d d6 ed a e3 34 d4 c3
  //   d3 0 d1 a d0 0 89 e0 67 f2 ab 8c 2a 2a d3 f3 ae d3 0 ee 58 d1 e0 3a a6 c7 d7 d1 e0 b6 8e a6 d7 d2 f2
  //   f5 a9 d7 d0 f3 b3 d0 40 4c e0 82 d6 51 f e5 78 d0 f 43 d7 c1 c3 d0 0 d3 9 8b e0 b3 f2 8c ba a e1 9c
  //   8c 8c ee 8f f1 8c b5 76 e0 a6 3a 8c ee 8f f1 8c b5 76 e0 af 3a ee 8f ee b3 ee 8f a e1 c0 d1 e0 b5 d3
  //   9 77 e1 c0 d2 3 c7 c5 d7 f 2f 2f 57 d1 21 16 fa 5b d0 f3 a3 d7 d6 6d d1 26 f5 ad d6 89 d6 c3 d7 d0
  //   18 d2 a 8a e0 ec f3 bd 5 e1 e9 ee ec 8c ee df d7 d6 6d d6 db d1 27 f5 ad d6 89 d6 c3 d7
endmodule

module TTT_Cell (
  input  [1:0] Hor_in,
  input  [1:0] Ver_in,
  input  reset,
  input  button,
  output [3:0] row0,
  output [3:0] row1,
  output [3:0] row2,
  output [3:0] row3,
  output Hor_out,
  output Ver_out
);

  wire and_1_out;
  wire [1:0] current_symbol_q;

  Pull_Resistor pull_resistor_1 (.node(Hor_in[1]));
  Pull_Resistor pull_resistor_2 (.node(Ver_in[1]));
  Transistor #(.\type ("n")) transistor_1 (.in(1'b0), .out(Hor_out), .gate(button));
  and and_1 (and_1_out, Hor_in[1], Ver_in[1]);
  Register #(.width(2), .trigger("high")) current_symbol (
    .D({Ver_in[0], Hor_in[0]}), .en(and_1_out), .Q(current_symbol_q), .clk(and_1_out), .clr(reset));
  ROM #(.addrWidth(2), .dataWidth(16)) rom_1 (.addr(current_symbol_q), .data({row3, row2, row1, row0}));  // open: sel

  assign Ver_out = Hor_out;

  // Notes on the sheet:
  //   symbol_ID
  //   address
  //   symbols
  //   bits
  //   contents of rom_1 (hex, n*v repeats v):
  //   0 9429 f99f 1234
endmodule

module Button_Press_Capture (
  input  button_reset,
  input  reset,
  input  Hor_bus0,
  input  Hor_bus1,
  input  Hor_bus2,
  input  Ver_bus0,
  input  Ver_bus1,
  input  Ver_bus2,
  input  end_of_game,
  output clean,
  output ready,
  output [3:0] XY
);

  wire and_1_out, and_2_out, and_3_out, and_4_out, buffer_1_out, buffer_4_out, not_1_out, not_2_out,
       not_3_out, not_4_out, not_5_out, not_6_out, not_7_out, not_8_out, not_9_out, not_10_out, or_1_out;
  wire [1:0] multiplexer_1_out, multiplexer_4_out;

  Multiplexer #(.width(2), .enable("false")) multiplexer_1 (
    .in0(2'b00), .out(multiplexer_1_out), .sel(Hor_bus0));  // open: in1
  buf buffer_1 (buffer_1_out, Hor_bus0);
  Multiplexer #(.width(2), .enable("false")) multiplexer_2 (
    .in0(2'b01), .out(multiplexer_1_out), .sel(Hor_bus1));  // open: in1
  Pull_Resistor #(.pull(1)) pull_resistor_1 (.node(buffer_1_out));
  buf buffer_2 (buffer_1_out, Hor_bus1);
  Multiplexer #(.width(2), .enable("false")) multiplexer_3 (
    .in0(2'b10), .out(multiplexer_1_out), .sel(Hor_bus2));  // open: in1
  buf buffer_3 (buffer_1_out, Hor_bus2);
  Multiplexer #(.width(2), .enable("false")) multiplexer_4 (
    .in0(2'b00), .out(multiplexer_4_out), .sel(Ver_bus0));  // open: in1
  buf buffer_4 (buffer_4_out, Ver_bus0);
  Multiplexer #(.width(2), .enable("false")) multiplexer_5 (
    .in0(2'b01), .out(multiplexer_4_out), .sel(Ver_bus1));  // open: in1
  buf buffer_5 (buffer_4_out, Ver_bus1);
  Pull_Resistor #(.pull(1)) pull_resistor_2 (.node(buffer_4_out));
  Multiplexer #(.width(2), .enable("false")) multiplexer_6 (
    .in0(2'b10), .out(multiplexer_4_out), .sel(Ver_bus2));  // open: in1
  buf buffer_6 (buffer_4_out, Ver_bus2);
  and and_1 (and_1_out, ~buffer_1_out, ~buffer_4_out, ~end_of_game);  // AND_Gate
  not not_1 (not_1_out, reset);
  and and_2 (and_2_out, button_reset, not_2_out);
  not not_2 (not_2_out, not_4_out);
  not not_3 (not_3_out, button_reset);
  not not_4 (not_4_out, not_3_out);
  not not_5 (not_5_out, not_7_out);
  not not_6 (not_6_out, and_1_out);
  not not_7 (not_7_out, not_6_out);
  not not_8 (not_8_out, not_10_out);
  not not_9 (not_9_out, not_1_out);
  not not_10 (not_10_out, not_9_out);
  Register #(.width(4), .trigger("high")) past_push (
    .D({multiplexer_4_out, multiplexer_1_out}), .en(and_1_out), .Q(XY), .clk(and_1_out));  // open: clr
  S_R_Flip_Flop clean_fl (.Q(clean), .preset(and_2_out), .reset(and_4_out));  // open: S, clk, R, Qn, en
  and and_3 (and_3_out, and_1_out, not_5_out);
  and and_4 (and_4_out, not_1_out, not_8_out);
  S_R_Flip_Flop ready_fl (.Q(ready), .preset(and_3_out), .reset(or_1_out));  // open: S, clk, R, Qn, en
  or or_1 (or_1_out, and_4_out, button_reset);

  // Notes on the sheet:
  //   y_crd
  //   xy_crd
  //   x_crd
  //   cell_press
endmodule

module Symbol_Display_Router (
  input  [1:0] Symbol_ID,
  input  sel,
  input  [3:0] xy_crd,
  output [1:0] Hor_bus0,
  output [1:0] Hor_bus1,
  output [1:0] Hor_bus2,
  output [1:0] Ver_bus0,
  output [1:0] Ver_bus1,
  output [1:0] Ver_bus2
);

  wire and_1_out, and_2_out, and_3_out, and_4_out, and_5_out, and_6_out, buffer_3_out, buffer_4_out,
       buffer_6_out, pull_resistor_1_node, pull_resistor_2_node, pull_resistor_5_node;

  Pull_Resistor #(.pull(1)) pull_resistor_1 (.node(pull_resistor_1_node));
  buf buffer_1 (pull_resistor_1_node, xy_crd[0]);
  Pull_Resistor pull_resistor_2 (.node(pull_resistor_2_node));
  buf buffer_2 (pull_resistor_2_node, xy_crd[0]);
  buf buffer_3 (buffer_3_out, xy_crd[0]);
  Pull_Resistor #(.pull(1)) pull_resistor_3 (.node(buffer_3_out));
  buf buffer_4 (buffer_4_out, xy_crd[2]);
  Pull_Resistor #(.pull(1)) pull_resistor_4 (.node(buffer_4_out));
  Pull_Resistor pull_resistor_5 (.node(pull_resistor_5_node));
  buf buffer_5 (pull_resistor_5_node, xy_crd[2]);
  buf buffer_6 (buffer_6_out, xy_crd[2]);
  Pull_Resistor #(.pull(1)) pull_resistor_6 (.node(buffer_6_out));
  and and_1 (and_1_out, ~pull_resistor_1_node, ~xy_crd[1]);  // AND_Gate
  and and_2 (and_2_out, pull_resistor_2_node, ~xy_crd[1]);  // AND_Gate
  and and_3 (and_3_out, ~buffer_3_out, xy_crd[1]);  // AND_Gate
  and and_4 (and_4_out, ~buffer_4_out, ~xy_crd[3]);  // AND_Gate
  and and_5 (and_5_out, pull_resistor_5_node, ~xy_crd[3]);  // AND_Gate
  and and_6 (and_6_out, ~buffer_6_out, xy_crd[3]);  // AND_Gate
  Multiplexer #(.width(2), .enable("false")) multiplexer_1 (
    .in1({sel, Symbol_ID[0]}), .out(Hor_bus0), .sel(and_1_out));  // open: in0
  Multiplexer #(.width(2), .enable("false")) multiplexer_2 (
    .in1({sel, Symbol_ID[0]}), .out(Hor_bus1), .sel(and_2_out));  // open: in0
  Multiplexer #(.width(2), .enable("false")) multiplexer_3 (
    .in1({sel, Symbol_ID[0]}), .out(Hor_bus2), .sel(and_3_out));  // open: in0
  Multiplexer #(.width(2), .enable("false")) multiplexer_4 (
    .in1({sel, Symbol_ID[1]}), .out(Ver_bus0), .sel(and_4_out));  // open: in0
  Multiplexer #(.width(2), .enable("false")) multiplexer_5 (
    .in1({sel, Symbol_ID[1]}), .out(Ver_bus1), .sel(and_5_out));  // open: in0
  Multiplexer #(.width(2), .enable("false")) multiplexer_6 (
    .in1({sel, Symbol_ID[1]}), .out(Ver_bus2), .sel(and_6_out));  // open: in0

  // Other names for the same wires on the sheet: Htrue[1:0] = {sel, Symbol_ID[0]}; Vtrue[1:0] = {sel, Symbol_ID[1]}

  // Notes on the sheet:
  //   x_crd
  //   y_crd
endmodule

module Game_State_Display_Driver (
  input  [1:0] result,
  input  sel,
  input  reset,
  output loss,
  output draw,
  output win,
  output end_of_game
);

  wire [1:0] state_q;

  Register #(.width(2), .trigger("high")) state (.D(result), .en(sel), .Q(state_q), .clk(sel), .clr(reset));
  and and_1 (loss, ~state_q[0], state_q[1]);  // AND_Gate
  and and_2 (draw, state_q[0], state_q[1]);
  and and_3 (win, state_q[0], ~state_q[1]);  // AND_Gate
  nand nand_1 (end_of_game, ~state_q[0], ~state_q[1]);  // NAND_Gate
endmodule

module Correctness_Turn_Driver (
  input  [7:0] IOdata,
  input  IOsel,
  input  [3:0] IOadr,
  input  reset,
  output good,
  output bad
);

  wire and_1_out;
  wire [1:0] turn_q;

  and and_1 (and_1_out, IOsel, ~IOadr[0], IOadr[1], ~IOadr[2], ~IOadr[3]);  // AND_Gate
  Register #(.width(2), .trigger("high")) turn (
    .D(IOdata[1:0]), .en(and_1_out), .Q(turn_q), .clk(and_1_out), .clr(reset));
  and and_2 (good, turn_q[0], ~turn_q[1]);  // AND_Gate
  and and_3 (bad, ~turn_q[0], turn_q[1]);  // AND_Gate

  // Notes on the sheet:
  //   00 - no turn
  //   01 - good turn
  //   10 - bad turn
  //   data_turn
  //   sel
endmodule
